// Logisim project RRISC.circ as structural Verilog: 7 circuits, main circuit main
module main (
);

  wire and_1_out, and_2_out, CARRY, clock_1_out, clock_2_out, comparator_1_eq, demultiplexer_1_out0,
       demultiplexer_1_out1, demultiplexer_1_out2, demultiplexer_1_out3, DONTSKIP, INST_RB, INST_WB, IsJump,
       IsSkip, MEM_WRITE, opcodedecoder_1_immmsb, opcodedecoder_1_isjump, opcodedecoder_1_notl,
       opcodedecoder_1_opbisimm, opcodedecoder_1_outrxid, opcodedecoder_1_r0, opcodedecoder_1_r1,
       opcodedecoder_1_r2, opcodedecoder_1_r3, opcodedecoder_1_swapnibbles, pc_1_boutajump, pc_1_boutaskip,
       RegisterWE, RST, SKIPME, WB, WRITEFLAG;
  wire [3:0] ACC_OUT_RX_WB, IMMEDIATE;
  wire [7:0] ALU_OUT_RESULT, MEM_DATA, MEMDATAIN, multiplexer_1_out, R0_ACC, RCD, RCS, register_1_q,
       register_2_q, register_3_q, register_4_q;
  wire [7:4] ram_1_data;
  wire [15:0] MEM_PC, REGS_OUT_MEM;

  Comparator #(.width(14)) comparator_1 (.a(14'h3c3c), .b(REGS_OUT_MEM[15:2]), .eq(comparator_1_eq));  // open: gt, lt
  and and_1 (and_1_out, MEM_WRITE, comparator_1_eq);
  Demultiplexer #(.enable("false"), .select(2)) demultiplexer_1 (
    .out0(demultiplexer_1_out0), .out1(demultiplexer_1_out1), .out2(demultiplexer_1_out2),
    .out3(demultiplexer_1_out3), .in(and_1_out), .sel(REGS_OUT_MEM[1:0]));
  // Probe on MEM_PC
  RAM #(.addrWidth(16), .clearpin("true"), .databus("bidir"), .trigger("high")) ram_1 (
    .addr(MEM_PC), .we(1'b0), .oe(1'b1), .data({ram_1_data, IMMEDIATE}));  // open: clr
  PC pc_1 (
    .IN_MEMREG(REGS_OUT_MEM), .IN_RCS(RCS), .IN_RCD(RCD), .IN_IMMEDIATE(IMMEDIATE), .IN_WB(WB), .IN_RST(RST),
    .IN_CARRYFLAG(CARRY), .IsJump(IsJump), .IsSkip(IsSkip), .MEMPC(MEM_PC), .BOUTAJUMP(pc_1_boutajump),
    .BOUTASKIP(pc_1_boutaskip));
  LED led_1 (.in(pc_1_boutajump));
  LED led_2 (.in(pc_1_boutaskip));
  D_Flip_Flop d_ff_1 (.D(pc_1_boutaskip), .clk(WB), .Qn(DONTSKIP));  // open: Q, preset, reset
  RAM #(.addrWidth(16), .clearpin("true"), .databus("bidir"), .trigger("high")) ram_2 (
    .addr(REGS_OUT_MEM), .we(MEM_WRITE), .oe(INST_RB), .data(MEM_DATA), .clr(RST));
  Clock clock_1 (.out(clock_1_out));
  Clock clock_2 (.out(clock_2_out));
  // Digital_Oscilloscope #(.nState(35)) digital_oscilloscope_1: pin names not known; wires that end beside it: clock_2_out, SKIPME, pc_1_boutajump
  Register register_1 (.D(MEMDATAIN), .en(demultiplexer_1_out0), .clk(WB), .Q(register_1_q), .clr(RST));
  Register register_2 (.D(MEMDATAIN), .en(demultiplexer_1_out1), .clk(WB), .Q(register_2_q), .clr(RST));
  Register register_3 (.D(MEMDATAIN), .en(demultiplexer_1_out2), .clk(WB), .Q(register_3_q), .clr(RST));
  Register register_4 (.D(MEMDATAIN), .en(demultiplexer_1_out3), .clk(WB), .Q(register_4_q), .clr(RST));
  Button BRST (.out(RST));
  // Probe on {ram_1_data, IMMEDIATE}
  Multiplexer #(.enable("false"), .width(8)) multiplexer_1 (
    .in0(ALU_OUT_RESULT), .in1(MEM_DATA), .out(multiplexer_1_out), .sel(INST_RB));
  and and_2 (and_2_out, RegisterWE, DONTSKIP);
  _7_Segment_Display u_7_segment_display_1 (
    .g(register_1_q[6]), .f(register_1_q[5]), .a(register_1_q[0]), .b(register_1_q[1]), .e(register_1_q[4]),
    .d(register_1_q[3]), .c(register_1_q[2]), .dp(register_1_q[7]));
  _7_Segment_Display u_7_segment_display_2 (
    .g(register_2_q[6]), .f(register_2_q[5]), .a(register_2_q[0]), .b(register_2_q[1]), .e(register_2_q[4]),
    .d(register_2_q[3]), .c(register_2_q[2]), .dp(register_2_q[7]));
  _7_Segment_Display u_7_segment_display_3 (
    .g(register_3_q[6]), .f(register_3_q[5]), .a(register_3_q[0]), .b(register_3_q[1]), .e(register_3_q[4]),
    .d(register_3_q[3]), .c(register_3_q[2]), .dp(register_3_q[7]));
  _7_Segment_Display u_7_segment_display_4 (
    .g(register_4_q[6]), .f(register_4_q[5]), .a(register_4_q[0]), .b(register_4_q[1]), .e(register_4_q[4]),
    .d(register_4_q[3]), .c(register_4_q[2]), .dp(register_4_q[7]));
  // Probe on multiplexer_1_out
  Controller controller_1 (.RST(RST), .CLK(clock_1_out), .EX(WB), .WB_ASYNC(WRITEFLAG));
  // Probe on ACC_OUT_RX_WB
  and and_3 (MEM_WRITE, INST_WB, DONTSKIP, WRITEFLAG);
  OpcodeDecoder opcodedecoder_1 (
    .OPCODE(ram_1_data), .RegisterWE(RegisterWE), .SwapNibbles(opcodedecoder_1_swapnibbles),
    .ImmMSB(opcodedecoder_1_immmsb), .R3(opcodedecoder_1_r3), .R2(opcodedecoder_1_r2),
    .R1(opcodedecoder_1_r1), .R0(opcodedecoder_1_r0), .NOTL(opcodedecoder_1_notl),
    .OutRXID(opcodedecoder_1_outrxid), .MemoryWrite(INST_WB), .MemoryRead(INST_RB),
    .OPBIsImm(opcodedecoder_1_opbisimm), .IsSkip(IsSkip), .IsJump(opcodedecoder_1_isjump));
  and and_4 (IsJump, opcodedecoder_1_isjump, DONTSKIP);
  // Probe on R0_ACC
  REGS regs_1 (
    .RST(RST), .Data(multiplexer_1_out), .CLK(WB), .Write(and_2_out), .Rx_Read(IMMEDIATE),
    .Rx_Write(ACC_OUT_RX_WB), .OUT_R0_ACC(R0_ACC), .OUT_REGDATA(MEMDATAIN), .OUT_RCS(RCS), .OUT_RCD(RCD),
    .OUT_MEM(REGS_OUT_MEM));
  // Probe on MEMDATAIN
  // Probe on RCS
  // Probe on RCD
  // Probe on REGS_OUT_MEM
  // Probe on R0_ACC
  assign MEM_DATA = INST_WB ? MEMDATAIN : 8'bz;  // Controlled_Buffer controlled_buffer_1
  MuxALU muxalu_1 (
    .REGDATA(MEMDATAIN), .IMM_MSB(opcodedecoder_1_immmsb), .IMMEDIATE(IMMEDIATE),
    .OPBIsImm(opcodedecoder_1_opbisimm), .NOTL(opcodedecoder_1_notl), .OutRxId(opcodedecoder_1_outrxid),
    .R3(opcodedecoder_1_r3), .R2(opcodedecoder_1_r2), .R1(opcodedecoder_1_r1), .R0(opcodedecoder_1_r0),
    .ACC(R0_ACC), .SwapNibbles(opcodedecoder_1_swapnibbles), .IN_WB_FLAGS(WB), .IN_RST_FLAGS(RST),
    .OUT_RX_WB(ACC_OUT_RX_WB), .RESULT(ALU_OUT_RESULT), .OUT_CARRY(CARRY));
  // Probe on ALU_OUT_RESULT
  // Probe on ALU_OUT_RESULT

  // Notes on the sheet:
  //   In=43 / Out=16
  //   Would be ANDed with its range,such as CE <= memory[13]
  //   An Example of Memory-Mapped IO
  //   11ns
  //   24ns
  //   EX: Spends cycle feeding-through ALU. Data clocked into WB at end.
  //   WE Pulled high for cycle. Writes to registers. Writes to memory if inst_memwrite
endmodule

module ALU (
  input  [7:0] IN_ACC,
  input  [3:0] OPCODE,
  input  [3:0] IN_IMMEDIATE,
  input  [7:0] REGDATA,
  input  IN_WB_FLAGS,
  input  IN_RST_FLAGS,
  output [7:0] OUT_RESULT,
  output [3:0] OUT_RX_WB,
  output OUT_CARRY
);

  wire and_1_out, and_2_out, demultiplexer_1_out2, demultiplexer_1_out4, demultiplexer_1_out5, FLAG_CARRY_IN,
       nor_1_out, not_1_out, or_1_out, or_3_out;
  wire [3:0] bit_extender_1_out, bit_extender_2_out;
  wire [7:0] adder_1_out, and_4_out, bit_extender_3_out, FULL_IMM, multiplexer_2_out, multiplexer_3_out,
       or_2_out, undriven, xor_1_out, xor_2_out;

  and and_1 (and_1_out, OPCODE[0], OPCODE[1], OPCODE[2]);
  and and_2 (and_2_out, OPCODE[1], OPCODE[2], OPCODE[3]);
  assign bit_extender_1_out = {{3{OPCODE[2]}}, OPCODE[2]};  // Bit_Extender bit_extender_1
  or or_1 (or_1_out, and_1_out, and_2_out);
  Multiplexer #(.enable("false"), .width(8)) multiplexer_1 (
    .in0({bit_extender_1_out, IN_IMMEDIATE}), .in1(REGDATA), .out(FULL_IMM), .sel(OPCODE[0]));
  assign bit_extender_2_out = {{3{or_1_out}}, or_1_out};  // Bit_Extender bit_extender_2
  assign OUT_RX_WB = IN_IMMEDIATE & bit_extender_2_out;  // AND_Gate and_3, 4 bits wide
  assign bit_extender_3_out = {{7{OPCODE[1]}}, OPCODE[1]};  // Bit_Extender bit_extender_3
  assign xor_1_out = bit_extender_3_out ^ FULL_IMM;  // XOR_Gate xor_1, 8 bits wide
  Adder adder_1 (.a(IN_ACC), .b(xor_1_out), .out(adder_1_out), .cin(OPCODE[1]), .cout(FLAG_CARRY_IN));
  assign and_4_out = IN_ACC & FULL_IMM;  // AND_Gate and_4, 8 bits wide
  Multiplexer #(.enable("false"), .width(8)) multiplexer_2 (
    .in0(REGDATA), .in1(IN_ACC), .out(multiplexer_2_out), .sel(OPCODE[0]));
  assign or_2_out = IN_ACC | FULL_IMM;  // OR_Gate or_2, 8 bits wide
  assign xor_2_out = IN_ACC ^ FULL_IMM;  // XOR_Gate xor_2, 8 bits wide
  nor nor_1 (nor_1_out, OPCODE[3], OPCODE[2]);
  Register #(.width(1)) FLAG_CARRY (
    .D(FLAG_CARRY_IN), .en(nor_1_out), .clk(IN_WB_FLAGS), .Q(OUT_CARRY), .clr(IN_RST_FLAGS));
  Multiplexer #(.enable("false"), .select(3), .width(8)) multiplexer_3 (
    .in0(adder_1_out), .in1(adder_1_out), .in2(and_4_out), .in3(multiplexer_2_out), .in4(or_2_out),
    .in5(xor_2_out), .in6(IN_ACC), .in7(undriven), .out(multiplexer_3_out), .sel(OPCODE[3:1]));
  not not_1 (not_1_out, OPCODE[0]);
  Demultiplexer #(.enable("false"), .select(3)) demultiplexer_1 (
    .out2(demultiplexer_1_out2), .out4(demultiplexer_1_out4), .out5(demultiplexer_1_out5), .in(not_1_out),
    .sel(OPCODE[3:1]));  // open: out0, out1, out3, out6, out7
  Multiplexer #(.enable("false"), .width(8)) multiplexer_4 (
    .in0(multiplexer_3_out), .in1({multiplexer_3_out[3:0], multiplexer_3_out[7:4]}), .out(OUT_RESULT),
    .sel(or_3_out));
  or or_3 (or_3_out, demultiplexer_1_out2, demultiplexer_1_out4, demultiplexer_1_out5);

  // Other names for the same wires on the sheet: IMMEDIATE[3:0] = IN_IMMEDIATE; OPCODE_LSB = OPCODE[0];
  //   OPCODE_BIT1 = OPCODE[1]

  // Notes on the sheet:
  //   If set, WB, or RB instruction: (DST=IMM) ELSE (DST=ACC)
  //   Data is register or immediate. The 4MSB of imm are 1s for AND and 0s for xor,add,or
  //   ANDI/AND
  //   GET/SET
  //   ORI/OR
  //   XORI/XOR
  //   WE = add/sub = opcode 0-3
  //   The actual ALU
  //   18.5ns
  //   ADDI/ADD/SUBI/SUB
  //   Has RST or WE
  //   SIF/JIF
  //   RB/WB
  //   14ns - 74HCS151
  //   Swap nibbles on imm and,or,xor
  //   Actual ALU Stuff
  //   ~40ns
endmodule

module REGS (
  input  RST,
  input  [7:0] Data,
  input  CLK,
  input  Write,
  input  [3:0] Rx_Read,
  input  [3:0] Rx_Write,
  output [7:0] OUT_R0_ACC,
  output [7:0] OUT_REGDATA,
  output [7:0] OUT_RCS,
  output [7:0] OUT_RCD,
  output [15:0] OUT_MEM
);

  wire demultiplexer_1_out0, demultiplexer_1_out1, demultiplexer_1_out2, demultiplexer_1_out3,
       demultiplexer_1_out4, demultiplexer_1_out5, demultiplexer_1_out6, demultiplexer_1_out7,
       demultiplexer_1_out8, demultiplexer_1_out9, demultiplexer_1_out10, demultiplexer_1_out11,
       demultiplexer_1_out12, demultiplexer_1_out13, demultiplexer_1_out14, demultiplexer_1_out15;
  wire [7:0] R1_q, R2_q, R3_q, R4_q, R5_q, R6_q, R7_q, R8_q, R9_RAT_q, RA_RSH_q, RB_RSL_q;

  Demultiplexer #(.enable("false"), .select(4)) demultiplexer_1 (
    .out0(demultiplexer_1_out0), .out1(demultiplexer_1_out1), .out2(demultiplexer_1_out2),
    .out3(demultiplexer_1_out3), .out4(demultiplexer_1_out4), .out5(demultiplexer_1_out5),
    .out6(demultiplexer_1_out6), .out7(demultiplexer_1_out7), .out8(demultiplexer_1_out8),
    .out9(demultiplexer_1_out9), .out10(demultiplexer_1_out10), .out11(demultiplexer_1_out11),
    .out12(demultiplexer_1_out12), .out13(demultiplexer_1_out13), .out14(demultiplexer_1_out14),
    .out15(demultiplexer_1_out15), .in(Write), .sel(Rx_Write));
  Register R0_ACC (.D(Data), .en(demultiplexer_1_out0), .clk(CLK), .Q(OUT_R0_ACC), .clr(RST));
  Register R1 (.D(Data), .en(demultiplexer_1_out1), .clk(CLK), .Q(R1_q), .clr(RST));
  Register R2 (.D(Data), .en(demultiplexer_1_out2), .clk(CLK), .Q(R2_q), .clr(RST));
  Register R3 (.D(Data), .en(demultiplexer_1_out3), .clk(CLK), .Q(R3_q), .clr(RST));
  Register R4 (.D(Data), .en(demultiplexer_1_out4), .clk(CLK), .Q(R4_q), .clr(RST));
  Register R5 (.D(Data), .en(demultiplexer_1_out5), .clk(CLK), .Q(R5_q), .clr(RST));
  Register R6 (.D(Data), .en(demultiplexer_1_out6), .clk(CLK), .Q(R6_q), .clr(RST));
  Register R7 (.D(Data), .en(demultiplexer_1_out7), .clk(CLK), .Q(R7_q), .clr(RST));
  Register R8 (.D(Data), .en(demultiplexer_1_out8), .clk(CLK), .Q(R8_q), .clr(RST));
  Register R9_RAT (.D(Data), .en(demultiplexer_1_out9), .clk(CLK), .Q(R9_RAT_q), .clr(RST));
  Register RA_RSH (.D(Data), .en(demultiplexer_1_out10), .clk(CLK), .Q(RA_RSH_q), .clr(RST));
  Register RB_RSL (.D(Data), .en(demultiplexer_1_out11), .clk(CLK), .Q(RB_RSL_q), .clr(RST));
  Register RC_RCS (.D(Data), .en(demultiplexer_1_out12), .clk(CLK), .Q(OUT_RCS), .clr(RST));
  Register RD_RCD (.D(Data), .en(demultiplexer_1_out13), .clk(CLK), .Q(OUT_RCD), .clr(RST));
  Register RE_RMH (.D(Data), .en(demultiplexer_1_out14), .clk(CLK), .Q(OUT_MEM[15:8]), .clr(RST));
  Register RF_RML (.D(Data), .en(demultiplexer_1_out15), .clk(CLK), .Q(OUT_MEM[7:0]), .clr(RST));
  Multiplexer #(.enable("false"), .select(4), .width(8)) multiplexer_1 (
    .in0(OUT_R0_ACC), .in1(R1_q), .in2(R2_q), .in3(R3_q), .in4(R4_q), .in5(R5_q), .in6(R6_q), .in7(R7_q),
    .in8(R8_q), .in9(R9_RAT_q), .in10(RA_RSH_q), .in11(RB_RSL_q), .in12(OUT_RCS), .in13(OUT_RCD),
    .in14(OUT_MEM[15:8]), .in15(OUT_MEM[7:0]), .out(OUT_REGDATA), .sel(Rx_Read));

  // Notes on the sheet:
  //   7xx154
  //   30ns
  //   6ns
  //   Has WE no RST, such as 74xx 377
  //   8x  7xx250
  //   Is actually 8 16:1 muxes
endmodule

module Controller (
  input  RST,
  input  CLK,
  output EX,
  output WB_ASYNC
);

  D_Flip_Flop d_ff_1 (.D(WB_ASYNC), .clk(CLK), .Q(EX), .preset(RST));  // open: Qn, reset
  D_Flip_Flop d_ff_2 (.D(EX), .clk(CLK), .Q(WB_ASYNC), .reset(RST));  // open: Qn, preset
endmodule

module PC (
  input  [15:0] IN_MEMREG,
  input  [7:0] IN_RCS,
  input  [7:0] IN_RCD,
  input  [3:0] IN_IMMEDIATE,
  input  IN_WB,
  input  IN_RST,
  input  IN_CARRYFLAG,
  input  IsJump,
  input  IsSkip,
  output [15:0] MEMPC,
  output BOUTAJUMP,
  output BOUTASKIP
);

  wire comparator_1_eq, comparator_1_gt, comparator_1_lt, multiplexer_1_out, or_1_out, undriven, undriven_2,
       xor_1_out;
  wire [0:0] not_1_out;
  wire [15:0] adder_1_out, multiplexer_2_out, register_1_q;

  Comparator #(.mode("unsigned")) comparator_1 (
    .a(IN_RCS), .b(IN_RCD), .gt(comparator_1_gt), .eq(comparator_1_eq), .lt(comparator_1_lt));
  or or_1 (or_1_out, IN_RCS[0], IN_RCS[1], IN_RCS[2], IN_RCS[3], IN_RCS[4], IN_RCS[5], IN_RCS[6], IN_RCS[7]);
  Multiplexer #(.enable("false"), .select(3)) multiplexer_1 (
    .in0(1'b1), .in1(or_1_out), .in2(IN_RCS[7]), .in3(comparator_1_lt), .in4(comparator_1_eq),
    .in5(comparator_1_gt), .in6(IN_RCS[0]), .in7(IN_CARRYFLAG), .out(multiplexer_1_out),
    .sel(IN_IMMEDIATE[3:1]));
  xor xor_1 (xor_1_out, multiplexer_1_out, IN_IMMEDIATE[0]);
  Register #(.width(16)) register_1 (
    .D(multiplexer_2_out), .en(1'b1), .clk(undriven), .Q(register_1_q), .clr(undriven_2));
  Multiplexer #(.enable("false"), .width(16)) multiplexer_2 (
    .in0(adder_1_out), .in1(IN_MEMREG), .out(multiplexer_2_out), .sel(BOUTAJUMP));
  not not_1 (not_1_out[0], BOUTASKIP);
  Adder #(.width(16)) adder_1 (
    .a(register_1_q), .b({{14{1'b0}}, BOUTASKIP, not_1_out[0]}), .out(adder_1_out));  // open: cin, cout
  and and_1 (BOUTAJUMP, xor_1_out, IsJump);
  and and_2 (BOUTASKIP, xor_1_out, IsSkip);
  Counter #(.max('hffff), .width(16)) counter_1 (
    .clr(IN_RST), .load(BOUTAJUMP), .up(1'b1), .count(1'b1), .clk(IN_WB), .D(IN_MEMREG), .Q(MEMPC));  // open: carry

  // Other names for the same wires on the sheet: ACC_OUT_IS_SKIP = BOUTASKIP; ACC_OUT_IS_JUMP = BOUTAJUMP;
  //   FLAG_CARRY_OUT = IN_CARRYFLAG; IMMEDIATE[3:0] = IN_IMMEDIATE; REGS_OUT_MEM[15:0] = IN_MEMREG

  // Notes on the sheet:
  //   Such as a 74xx 684 with a NAND for >
  //   12ns
  //   17ns
  //   Branch Event
  //   Has RST no WE, such as 74xx 273
  //   Branch event and instruction
  //   34ns - 74xx283
  //   PC+1 or PC+2
  //   5ns
  //   ~40ns
endmodule

module MuxALU (
  input  [7:0] REGDATA,
  input  IMM_MSB,
  input  [3:0] IMMEDIATE,
  input  OPBIsImm,
  input  NOTL,
  input  OutRxId,
  input  R3,
  input  R2,
  input  R1,
  input  R0,
  input  [7:0] ACC,
  input  SwapNibbles,
  input  IN_WB_FLAGS,
  input  IN_RST_FLAGS,
  output [3:0] OUT_RX_WB,
  output [7:0] RESULT,
  output OUT_CARRY
);

  wire adder_1_cout, L;
  wire [3:0] bit_extender_1_out, bit_extender_2_out;
  wire [7:0] adder_1_out, multiplexer_1_out, multiplexer_2_out, OPB;

  Multiplexer #(.enable("false"), .select(2)) multiplexer_1 (
    .in0(R0), .in1(R1), .in2(R2), .in3(R3), .out(multiplexer_1_out[0]), .sel({OPB[0], ACC[0]}));
  Multiplexer #(.select(2)) multiplexer_2 (
    .in0(1'b0), .in1(1'b1), .in2(1'b0), .in3(1'b1), .out(multiplexer_2_out[0]), .sel({OPB[0], ACC[0]}), .en(L));
  not not_1 (L, NOTL);
  Multiplexer #(.enable("false"), .select(2)) multiplexer_3 (
    .in0(R0), .in1(R1), .in2(R2), .in3(R3), .out(multiplexer_1_out[1]), .sel({OPB[1], ACC[1]}));
  Multiplexer #(.select(2)) multiplexer_4 (
    .in0(1'b0), .in1(1'b1), .in2(1'b0), .in3(1'b1), .out(multiplexer_2_out[1]), .sel({OPB[1], ACC[1]}), .en(L));
  Multiplexer #(.enable("false"), .select(2)) multiplexer_5 (
    .in0(R0), .in1(R1), .in2(R2), .in3(R3), .out(multiplexer_1_out[2]), .sel({OPB[2], ACC[2]}));
  Multiplexer #(.select(2)) multiplexer_6 (
    .in0(1'b0), .in1(1'b1), .in2(1'b0), .in3(1'b1), .out(multiplexer_2_out[2]), .sel({OPB[2], ACC[2]}), .en(L));
  assign bit_extender_1_out = {{3{IMM_MSB}}, IMM_MSB};  // Bit_Extender bit_extender_1
  assign bit_extender_2_out = {{3{OutRxId}}, OutRxId};  // Bit_Extender bit_extender_2
  Multiplexer #(.enable("false"), .select(2)) multiplexer_7 (
    .in0(R0), .in1(R1), .in2(R2), .in3(R3), .out(multiplexer_1_out[3]), .sel({OPB[3], ACC[3]}));
  Multiplexer #(.select(2)) multiplexer_8 (
    .in0(1'b0), .in1(1'b1), .in2(1'b0), .in3(1'b1), .out(multiplexer_2_out[3]), .sel({OPB[3], ACC[3]}), .en(L));
  assign OUT_RX_WB = IMMEDIATE & bit_extender_2_out;  // AND_Gate and_1, 4 bits wide
  Multiplexer #(.enable("false"), .select(2)) multiplexer_9 (
    .in0(R0), .in1(R1), .in2(R2), .in3(R3), .out(multiplexer_1_out[4]), .sel({OPB[4], ACC[4]}));
  Multiplexer #(.select(2)) multiplexer_10 (
    .in0(1'b0), .in1(1'b1), .in2(1'b0), .in3(1'b1), .out(multiplexer_2_out[4]), .sel({OPB[4], ACC[4]}), .en(L));
  Multiplexer #(.enable("false"), .width(8)) multiplexer_11 (
    .in0(REGDATA), .in1({bit_extender_1_out, IMMEDIATE}), .out(OPB), .sel(OPBIsImm));
  Multiplexer #(.enable("false"), .select(2)) multiplexer_12 (
    .in0(R0), .in1(R1), .in2(R2), .in3(R3), .out(multiplexer_1_out[5]), .sel({OPB[5], ACC[5]}));
  Multiplexer #(.select(2)) multiplexer_13 (
    .in0(1'b0), .in1(1'b1), .in2(1'b0), .in3(1'b1), .out(multiplexer_2_out[5]), .sel({OPB[5], ACC[5]}), .en(L));
  Multiplexer #(.enable("false"), .select(2)) multiplexer_14 (
    .in0(R0), .in1(R1), .in2(R2), .in3(R3), .out(multiplexer_1_out[6]), .sel({OPB[6], ACC[6]}));
  Multiplexer #(.select(2)) multiplexer_15 (
    .in0(1'b0), .in1(1'b1), .in2(1'b0), .in3(1'b1), .out(multiplexer_2_out[6]), .sel({OPB[6], ACC[6]}), .en(L));
  Multiplexer #(.enable("false"), .select(2)) multiplexer_16 (
    .in0(R0), .in1(R1), .in2(R2), .in3(R3), .out(multiplexer_1_out[7]), .sel({OPB[7], ACC[7]}));
  Multiplexer #(.select(2)) multiplexer_17 (
    .in0(1'b0), .in1(1'b1), .in2(1'b0), .in3(1'b1), .out(multiplexer_2_out[7]), .sel({OPB[7], ACC[7]}), .en(L));
  Adder adder_1 (.a(multiplexer_1_out), .b(multiplexer_2_out), .out(adder_1_out), .cin(R0), .cout(adder_1_cout));
  Multiplexer #(.enable("false"), .width(8)) multiplexer_18 (
    .in0(adder_1_out), .in1({adder_1_out[3:0], adder_1_out[7:4]}), .out(RESULT), .sel(SwapNibbles));
  Register #(.width(1)) register_1 (.D(adder_1_cout), .en(L), .clk(IN_WB_FLAGS), .Q(OUT_CARRY), .clr(IN_RST_FLAGS));
endmodule

module OpcodeDecoder (
  input  [3:0] OPCODE,
  output RegisterWE,
  output SwapNibbles,
  output ImmMSB,
  output R3,
  output R2,
  output R1,
  output R0,
  output NOTL,
  output OutRXID,
  output MemoryWrite,
  output MemoryRead,
  output OPBIsImm,
  output IsSkip,
  output IsJump
);

  wire decoder_1_out0, decoder_1_out2, decoder_1_out6, nand_1_out, not_3_out, or_3_out;

  Decoder #(.select(3)) decoder_1 (
    .out0(decoder_1_out0), .out1(R0), .out2(decoder_1_out2), .out4(ImmMSB), .out5(OutRXID),
    .out6(decoder_1_out6), .sel(OPCODE[3:1]));  // open: out3, out7, en
  or or_1 (NOTL, OPCODE[3], OPCODE[2]);
  or or_2 (R2, OPCODE[2], decoder_1_out0);
  or or_3 (or_3_out, MemoryWrite, decoder_1_out2);
  or or_4 (R3, decoder_1_out0, OPCODE[3]);
  and and_1 (SwapNibbles, OPCODE[0], NOTL);
  and and_2 (IsJump, OPCODE[0], decoder_1_out2);
  and and_3 (MemoryWrite, OPCODE[0], decoder_1_out6);
  and and_4 (MemoryRead, OPCODE[0], OutRXID);
  not not_1 (RegisterWE, or_3_out);
  not not_2 (IsSkip, nand_1_out);
  nand nand_1 (nand_1_out, decoder_1_out2, not_3_out);
  not not_3 (not_3_out, OPCODE[0]);

  assign OPBIsImm = OPCODE[0];
  assign R1 = OPCODE[1];

  // Notes on the sheet:
  //   A
  //   B
  //   C
  //   D
  //   E
  //   F
  //   G
  //   H
  //   I
  //   jay
  //   K
  //   L
  //   M
  //   N
  //   R0 is carry
  //   This op changes registers
  //   The ALU should swap nibbles
  //   R is the ALU instruction
  //   Don't edit carry. Don't add acc
  //   Write this to IMM
  //   Set memory read line high.
  //   The ALU should use this as the upper IMM nibble
  //   Set memory write line high. Put reg into memory
  //   Second ALU Inst is from IMM
endmodule
